# Fritzing sketch scroller-fritzing (saved by Fritzing 1.0.3b)
breadboards: 1

parts:
  Raspberry_Pi_1 = Raspberry Pi 3 [part_number=RPI-3-V1.2]
  Part1 = ADS1115
  U1 = POT [knob_status=50% power=0.5W package=pot_alpha_rv16af-20]
  U2 = POT [knob_status=50% power=0.5W package=pot_alpha_rv16af-20]

nets:
  N1: Raspberry_Pi_1.GPIO2, Part1.SDA
  N2: Raspberry_Pi_1.GPIO3, Part1.SCL
  GND: Raspberry_Pi_1.GND, Part1.GND, U1.E, U2.E
  N3: Raspberry_Pi_1.3V3, U1.A, U2.A
  5V: Raspberry_Pi_1.5V, Part1.VDD
  N4: Part1.A0, U1.S
  N5: Part1.A1, U2.S

custom parts:
  ADS1115: ADC ADS1115
